# Fritzing sketch TiltandEcho (saved by Fritzing 0.9.3b)
breadboards: 1

parts:
  S1 = Tilt Switch [package=THT]
  Part1 = Arduino Uno (Rev3)
  hc-sr1 = hc-sr04
  S2 = Pushbutton [package="[THT]"]

nets:
  GND: S1.Pin_1, S1.Pin_2, Part1.D3_PWM, Part1.GND, hc-sr1.GND, S2.Pin_1, S2.Pin_2
  N1: Part1.D6_PWM, hc-sr1.Trig
  N2: Part1.D7, hc-sr1.Echo
  N3: Part1.RESET, S2.Pin_3, S2.Pin_4
  5V: Part1.5V, hc-sr1.VCC
