# Fritzing sketch padlock_sketch (saved by Fritzing 0.9.3b)
breadboards: 1

parts:
  Part1 = Arduino Uno (Rev3)
  R1 = PHOTOCELL [package=photocell-kit]
  R2 = PHOTOCELL [package=photocell-kit]
  R3 = PHOTOCELL [package=photocell-kit]
  R4 = Resistor [tolerance=±5% resistance=10 package="0805 [SMD]"]  # not connected
  R5 = Resistor [tolerance=±5% resistance=10 package="0402 [SMD]"]
  R6 = Resistor [tolerance=±5% resistance=10 package="0402 [SMD]"]
  R7 = Resistor [tolerance=±5% resistance=10 package="0402 [SMD]"]
  R8 = Resistor [tolerance=±5% resistance=10 package="0402 [SMD]"]
  R9 = Resistor [tolerance=±5% resistance=10 package="1206 [SMD]"]
  R10 = Resistor [tolerance=±5% resistance=100 package="1206 [SMD]"]
  LED1 = LED - 5mm [color="Red (633nm)" package="5 mm [THT]"]
  LED2 = LED - 5mm [color="Yellow (585nm)" package="5 mm [THT]"]
  LED3 = LED - 5mm [color="Green (560nm)" package="5 mm [THT]"]
  LED4 = LED - 5mm [color="Blue (505nm)" package="5 mm [THT]"]

nets:
  N1: Part1.A0, R1.P$2, R6.Pin_1
  N2: Part1.A1, R2.P$2, R5.Pin_1
  N3: Part1.A2, R3.P$2
  N4: Part1.D8, R8.Pin_0
  N5: Part1.D10_PWM/SS, R9.Pin_0
  N6: Part1.D13/SCK, R10.Pin_0
  N7: Part1.D7, R7.Pin_0
  N8: Part1.5V, R1.P$1, R2.P$1, R3.P$1
  N9: Part1.GND, R5.Pin_0, R6.Pin_0, LED1.cathode, LED2.cathode, LED3.cathode, LED4.cathode
  N10: R7.Pin_1, LED3.anode
  N11: R8.Pin_1, LED1.anode
  N12: R9.Pin_1, LED4.anode
  N13: R10.Pin_1, LED2.anode

// code stored in the sketch: padlock_test.ino
//For teting light per side

#define GREEN 7
#define BLUE 10
#define RED 8
#define LED 13
int left_cal=250;
int right_cal=250;
int center_cal=250;

int left_light;
int right_light;  
int center_light;

char code[4];


void setup() {
  pinMode(GREEN, OUTPUT);
  pinMode(BLUE,OUTPUT);
  pinMode(RED, OUTPUT);
  pinMode(LED,OUTPUT);
  //run once with serial moniter on to find baseline light levels and set these
  //a little higher so flashlights will set them off
  //



  

  Serial.begin(9600);

}

void print_calibrations(){
  Serial.write("center: ");
  Serial.println(center_light);
  Serial.write("right: ");
  Serial.println(right_light);
  Serial.write("left: ");
  Serial.println(left_light);
  
}

bool is_order(char code[4])
{
  //Set this to the vaule you want for the combo lock
  //c=center, r=right l=left, use lowercase
  char ans[4]="rrrr";
  
  bool ret=false;
  
  for(int i=0;i<4;i++)
  {
    if(code[i]!=ans[i])
    {
      ret=false;
      Serial.print(i);
      Serial.print(code[i]);
      Serial.println(ans[i]);
      break;
    }
    else ret=true;    
  }
  
  return ret;
}

char censor_check()
{
  char ans;
  if(left_light > left_cal){
    ans='l';
    digitalWrite(GREEN,HIGH);
    delay(500);
    digitalWrite(GREEN,LOW);
  }
  else if(right_light > right_cal){
    ans='r';
    digitalWrite(BLUE,HIGH);
    delay(500);
    
    digitalWrite(BLUE,LOW);
  }
  else if(center_light > center_cal){
    ans='c';
    digitalWrite(RED,HIGH);
    delay(500);
    digitalWrite(RED,LOW);
    
  }
  else ans='f';
  delay(1500);
  return ans;
}

void loop() {  
  
  left_light = analogRead(A0);
  right_light = analogRead(A2);
  center_light=analogRead(A1);
  
  //this will print the current values for light sensor
  print_calibrations();
  
  for(int i=0;i<4;++i){
    code[i]=censor_check();
    delay(1500);
    /*
    while(code[i]=='f')
    {
      code[i]=censor_check();    
    }
    */    
  }
  if(is_order(code)==true){
    digitalWrite(LED,HIGH);
    Serial.write("Code is true");
  }
}
